# Fritzing sketch AtxPwr (saved by Fritzing 0.7.0b)
stripboards: 1

parts:
  DC-DC_5-3_6V_1 = DCDC Converter [package=THT]
  PowerFromATXStandbyWires = female pin header, 2 pins [form="♀ (female)"]
  MSP430 = DIP - 16 pins [package="DIP (Dual Inline) [THT]"]
  R1 = Resistor [tolerance=±5% resistance=220 package=THT]
  R2 = Resistor [tolerance=±5% resistance=220 package=THT]
  RedHDConnectorWire = female pin header, 1 pin [form="♀ (female)"]
  BlackHDConnector_Wire = female pin header, 1 pin [form="♀ (female)"]
  Pulldown = Resistor [tolerance=±5% resistance=220 package=THT]
  Q1 = NPN-Transistor [package="TO92 [THT]"]
  R4 = Resistor [tolerance=±5% resistance=220 package=THT]
  R5 = Resistor [tolerance=±5% resistance=220 package=THT]
  LED1 = LED - 5mm [color="Red (633nm)" package="5 mm [THT]"]
  PullUp = Resistor [tolerance=±5% resistance=10k package=THT]
  D1 = Rectifier Diode [part_number=1N4001 package="300 mil [THT]"]
  R7 = Resistor [tolerance=±5% resistance=220 package=THT]
  Q2 = PNP-Transistor [package="TO92 [THT]"]
  R8 = Resistor [tolerance=±5% resistance=220 package=THT]
  PowerSwitchOnMotherBoard = female pin header, 2 pins [form="♀ (female)"]
  PowerSwitchOnChasis = female pin header, 2 pins [form="♀ (female)"]

nets:
  N1: DC-DC_5-3_6V_1.-V_Input, DC-DC_5-3_6V_1.-V_Output, PowerFromATXStandbyWires.pin1, MSP430.pin16, Pulldown.Pin_0, LED1.cathode
  N2: DC-DC_5-3_6V_1.+V_Input, PowerFromATXStandbyWires.pin2
  N3: DC-DC_5-3_6V_1.+V_Output, MSP430.pin1, Q1.C, PullUp.Pin_1
  N4: MSP430.pin2, R4.Pin_1
  N5: MSP430.pin6, R1.Pin_0, R2.Pin_0, Pulldown.Pin_1
  N6: MSP430.pin9, R7.Pin_0
  N7: MSP430.pin13, PullUp.Pin_0
  N8: R1.Pin_1, RedHDConnectorWire.pin1
  N9: R2.Pin_1, BlackHDConnector_Wire.pin1
  N10: Q1.E, R5.Pin_0
  N11: Q1.B, R4.Pin_0
  N12: R5.Pin_1, LED1.anode
  N13: D1.cathode, R8.Pin_0
  N14: D1.anode, PowerSwitchOnMotherBoard.pin1, PowerSwitchOnChasis.pin2
  N15: R7.Pin_1, Q2.B
  N16: Q2.E, R8.Pin_1
  N17: Q2.C, PowerSwitchOnMotherBoard.pin2, PowerSwitchOnChasis.pin1

custom parts:
  DCDC Converter: A dummy, proxy, ersatz, stand-in part for whatever you want. With 4 pins on a 100 mil inline pin header footprint.
  DIP - 16 pins: A DIP stand-in part for whatever IC you want. With 16 pins on a 300 mil dual inline package (DIP) footprint.
